// Logisim project Sumador 8 bits.circ as structural Verilog: 1 circuit, main circuit main
module main (
  input  [7:0] in_1,
  input  [7:0] in_2,
  input  Cin,
  output [8:0] out_4
);

  wire and_1_out, and_2_out, and_3_out, and_4_out, and_5_out, and_6_out, and_7_out, and_8_out, and_9_out,
       and_10_out, and_11_out, and_12_out, and_13_out, and_14_out, and_15_out, and_16_out, or_1_out,
       or_2_out, or_3_out, or_4_out, or_5_out, or_6_out, or_7_out, or_8_out, xor_2_out, xor_3_out, xor_5_out,
       xor_6_out, xor_8_out, xor_9_out, xor_11_out, xor_12_out, xor_14_out, xor_15_out, xor_17_out,
       xor_18_out, xor_20_out, xor_21_out, xor_23_out, xor_24_out;

  and and_1 (and_1_out, in_1[7], xor_2_out);
  or or_1 (or_1_out, and_1_out, and_2_out);
  xor xor_1 (out_4[8], Cin, or_1_out);
  xor xor_2 (xor_2_out, Cin, in_2[7]);
  xor xor_3 (xor_3_out, in_1[7], xor_2_out);
  xor xor_4 (out_4[7], xor_3_out, or_2_out);
  and and_2 (and_2_out, xor_3_out, or_2_out);
  and and_3 (and_3_out, in_1[6], xor_5_out);
  or or_2 (or_2_out, and_3_out, and_4_out);
  xor xor_5 (xor_5_out, Cin, in_2[6]);
  xor xor_6 (xor_6_out, in_1[6], xor_5_out);
  xor xor_7 (out_4[6], xor_6_out, or_3_out);
  and and_4 (and_4_out, xor_6_out, or_3_out);
  and and_5 (and_5_out, in_1[5], xor_8_out);
  or or_3 (or_3_out, and_5_out, and_6_out);
  xor xor_8 (xor_8_out, Cin, in_2[5]);
  xor xor_9 (xor_9_out, in_1[5], xor_8_out);
  xor xor_10 (out_4[5], xor_9_out, or_4_out);
  and and_6 (and_6_out, xor_9_out, or_4_out);
  and and_7 (and_7_out, in_1[4], xor_11_out);
  or or_4 (or_4_out, and_7_out, and_8_out);
  xor xor_11 (xor_11_out, Cin, in_2[4]);
  xor xor_12 (xor_12_out, in_1[4], xor_11_out);
  xor xor_13 (out_4[4], xor_12_out, or_5_out);
  and and_8 (and_8_out, xor_12_out, or_5_out);
  and and_9 (and_9_out, in_1[3], xor_14_out);
  or or_5 (or_5_out, and_9_out, and_10_out);
  xor xor_14 (xor_14_out, Cin, in_2[3]);
  xor xor_15 (xor_15_out, in_1[3], xor_14_out);
  xor xor_16 (out_4[3], xor_15_out, or_6_out);
  and and_10 (and_10_out, xor_15_out, or_6_out);
  and and_11 (and_11_out, in_1[2], xor_17_out);
  or or_6 (or_6_out, and_11_out, and_12_out);
  xor xor_17 (xor_17_out, Cin, in_2[2]);
  xor xor_18 (xor_18_out, in_1[2], xor_17_out);
  xor xor_19 (out_4[2], xor_18_out, or_7_out);
  and and_12 (and_12_out, xor_18_out, or_7_out);
  and and_13 (and_13_out, in_1[1], xor_20_out);
  or or_7 (or_7_out, and_13_out, and_14_out);
  xor xor_20 (xor_20_out, Cin, in_2[1]);
  xor xor_21 (xor_21_out, in_1[1], xor_20_out);
  xor xor_22 (out_4[1], xor_21_out, or_8_out);
  and and_14 (and_14_out, xor_21_out, or_8_out);
  and and_15 (and_15_out, in_1[0], xor_23_out);
  or or_8 (or_8_out, and_15_out, and_16_out);
  xor xor_23 (xor_23_out, Cin, in_2[0]);
  xor xor_24 (xor_24_out, in_1[0], xor_23_out);
  xor xor_25 (out_4[0], xor_24_out, Cin);
  and and_16 (and_16_out, xor_24_out, Cin);
endmodule
